// Logisim project new_min.circ as structural Verilog: 2 circuits, main circuit test
module test (
  input  x1,
  input  x2,
  input  x3,
  input  x4,
  output a,
  output b,
  output c,
  output d,
  output e,
  output f,
  output g
);

  wire and_1_out, and_2_out, and_3_out, and_4_out, and_5_out, and_6_out, and_7_out, and_8_out, not_1_out,
       not_2_out, not_3_out, not_4_out, not_5_out, not_6_out, not_7_out, not_8_out, not_9_out, not_10_out,
       not_11_out, not_12_out, not_13_out, not_14_out, not_15_out, not_16_out, not_17_out, not_18_out,
       not_19_out, not_20_out, not_21_out, not_22_out, or_1_out, or_2_out, or_4_out, or_5_out, or_6_out,
       or_7_out, or_8_out;

  not not_1 (not_1_out, x4);
  not not_2 (not_2_out, x2);
  not not_3 (not_3_out, x2);
  or or_1 (or_1_out, not_3_out, x3, not_4_out);
  not not_4 (not_4_out, x4);
  not not_5 (not_5_out, x2);
  or or_2 (or_2_out, not_5_out, not_6_out, x4);
  not not_6 (not_6_out, x3);
  or or_3 (c, x2, not_7_out, x4);
  not not_7 (not_7_out, x3);
  not not_8 (not_8_out, x4);
  not not_9 (not_9_out, x2);
  not not_10 (not_10_out, x2);
  not not_11 (not_11_out, x3);
  not not_12 (not_12_out, x4);
  not not_13 (not_13_out, x2);
  and and_1 (and_1_out, not_13_out, not_14_out);
  not not_14 (not_14_out, x4);
  and and_2 (and_2_out, x3, not_15_out);
  not not_15 (not_15_out, x4);
  not not_16 (not_16_out, x3);
  and and_3 (and_3_out, not_16_out, not_17_out);
  not not_17 (not_17_out, x4);
  and and_4 (and_4_out, x2, not_18_out);
  not not_18 (not_18_out, x3);
  and and_5 (and_5_out, x2, not_19_out);
  not not_19 (not_19_out, x4);
  not not_20 (not_20_out, x2);
  and and_6 (and_6_out, not_20_out, x3);
  and and_7 (and_7_out, x2, not_21_out);
  not not_21 (not_21_out, x3);
  and and_8 (and_8_out, x2, not_22_out);
  not not_22 (not_22_out, x4);
  or or_4 (or_4_out, x1, x2, x3, not_1_out);
  and and_9 (a, or_4_out, or_5_out);
  or or_5 (or_5_out, not_2_out, x3, x4);
  and and_10 (b, or_1_out, or_2_out);
  or or_6 (or_6_out, x1, x2, x3, not_8_out);
  or or_7 (or_7_out, not_9_out, x3, x4);
  and and_11 (d, or_6_out, or_7_out, or_8_out);
  or or_8 (or_8_out, not_10_out, not_11_out, not_12_out);
  or or_9 (e, and_1_out, and_2_out);
  or or_10 (f, and_3_out, and_4_out, and_5_out, x1);
  or or_11 (g, and_6_out, and_7_out, and_8_out, x1);
endmodule

module my (
  input  x1,
  input  x2,
  input  x3,
  input  x4,
  output a,
  output b,
  output c,
  output d,
  output e,
  output f,
  output g
);

  wire and_1_out, and_2_out, and_3_out, and_4_out, and_5_out, and_6_out, and_7_out, and_8_out, and_9_out,
       and_10_out, and_11_out, and_12_out, and_13_out, and_14_out, not_1_out, not_2_out, not_3_out,
       not_4_out, not_5_out, not_6_out, not_7_out, not_8_out, not_9_out, not_10_out, not_11_out, not_12_out,
       not_13_out, not_14_out, not_15_out, not_16_out, not_17_out, not_18_out, not_19_out, not_20_out,
       not_21_out, not_22_out, not_23_out, not_24_out, not_25_out, not_26_out, not_27_out, not_28_out,
       not_29_out, not_30_out, not_31_out, not_32_out, not_33_out, not_34_out, not_35_out, not_36_out,
       not_37_out, not_38_out, not_39_out, not_40_out, not_41_out, not_42_out, not_43_out, not_44_out,
       or_1_out, or_2_out, or_3_out, or_4_out, or_5_out, or_6_out, or_7_out, or_8_out, or_9_out, or_10_out,
       or_11_out, or_12_out, or_13_out, or_14_out, or_15_out;

  not not_1 (not_1_out, x4);
  not not_2 (not_2_out, x2);
  not not_3 (not_3_out, x1);
  not not_4 (not_4_out, x3);
  not not_5 (not_5_out, x4);
  not not_6 (not_6_out, x1);
  not not_7 (not_7_out, x2);
  not not_8 (not_8_out, x4);
  not not_9 (not_9_out, x2);
  not not_10 (not_10_out, x4);
  not not_11 (not_11_out, x2);
  not not_12 (not_12_out, x3);
  not not_13 (not_13_out, x1);
  not not_14 (not_14_out, x3);
  not not_15 (not_15_out, x4);
  not not_16 (not_16_out, x1);
  not not_17 (not_17_out, x2);
  not not_18 (not_18_out, x3);
  not not_19 (not_19_out, x1);
  not not_20 (not_20_out, x2);
  not not_21 (not_21_out, x1);
  not not_22 (not_22_out, x2);
  not not_23 (not_23_out, x3);
  not not_24 (not_24_out, x4);
  not not_25 (not_25_out, x2);
  not not_26 (not_26_out, x2);
  not not_27 (not_27_out, x3);
  not not_28 (not_28_out, x4);
  not not_29 (not_29_out, x1);
  not not_30 (not_30_out, x3);
  not not_31 (not_31_out, x2);
  and and_1 (and_1_out, not_31_out, not_32_out);
  not not_32 (not_32_out, x4);
  and and_2 (and_2_out, x3, not_33_out);
  not not_33 (not_33_out, x4);
  and and_3 (and_3_out, x1, x3);
  and and_4 (and_4_out, x1, x2);
  not not_34 (not_34_out, x3);
  and and_5 (and_5_out, not_34_out, not_35_out);
  not not_35 (not_35_out, x4);
  not not_36 (not_36_out, x1);
  and and_6 (and_6_out, not_36_out, x2, not_37_out);
  not not_37 (not_37_out, x3);
  and and_7 (and_7_out, x2, not_38_out);
  not not_38 (not_38_out, x4);
  and and_8 (and_8_out, x1, not_39_out);
  not not_39 (not_39_out, x2);
  and and_9 (and_9_out, x1, x3);
  not not_40 (not_40_out, x2);
  and and_10 (and_10_out, not_40_out, x3);
  and and_11 (and_11_out, x3, not_41_out);
  not not_41 (not_41_out, x4);
  not not_42 (not_42_out, x1);
  and and_12 (and_12_out, not_42_out, x2, not_43_out);
  not not_43 (not_43_out, x3);
  and and_13 (and_13_out, x1, not_44_out);
  not not_44 (not_44_out, x2);
  and and_14 (and_14_out, x1, x4);
  or or_1 (or_1_out, x1, x2, x3, not_1_out);
  or or_2 (or_2_out, x1, not_2_out, x3, x4);
  or or_3 (or_3_out, not_3_out, x2, not_4_out, not_5_out);
  or or_4 (or_4_out, not_6_out, not_7_out, x3, not_8_out);
  or or_5 (or_5_out, x1, not_9_out, x3, not_10_out);
  or or_6 (or_6_out, not_11_out, not_12_out, x4);
  or or_7 (or_7_out, not_13_out, not_14_out, not_15_out);
  or or_8 (or_8_out, not_16_out, not_17_out, x4);
  or or_9 (or_9_out, x1, x2, not_18_out, x4);
  and and_15 (c, or_9_out, or_10_out, or_11_out);
  or or_10 (or_10_out, not_19_out, not_20_out, x4);
  or or_11 (or_11_out, not_21_out, not_22_out, not_23_out);
  or or_12 (or_12_out, x1, x2, x3, not_24_out);
  or or_13 (or_13_out, x1, not_25_out, x3, x4);
  or or_14 (or_14_out, not_26_out, not_27_out, not_28_out);
  or or_15 (or_15_out, not_29_out, x2, not_30_out, x4);
  or or_16 (e, and_1_out, and_2_out, and_3_out, and_4_out);
  or or_17 (f, and_5_out, and_6_out, and_7_out, and_8_out, and_9_out);
  or or_18 (g, and_10_out, and_11_out, and_12_out, and_13_out, and_14_out);
  and and_16 (a, or_1_out, or_2_out, or_3_out, or_4_out);
  and and_17 (b, or_5_out, or_6_out, or_7_out, or_8_out);
  and and_18 (d, or_12_out, or_13_out, or_14_out, or_15_out);
endmodule
